# Fritzing sketch brushless_control_rs485 (saved by Fritzing 0.9.3b)
breadboards: 2

parts:
  U1 = MAX485 [package=dil08]  # not connected
  U2 = MAX485 [package=dil08]  # not connected
  Part1 = Arduino Uno (Rev3)
  Part2 = Arduino Mega 2560 (Rev3)
  J1 = Basic Servo
  S1 = Momentary Switch [package=ksa_sealed_tac_switch]
  S2 = Momentary Switch [package=ksa_sealed_tac_switch]
  R1 = Resistor [tolerance=±5% resistance=10k package="2010 [SMD]"]
  R2 = Resistor [tolerance=±5% resistance=10k package="2010 [SMD]"]

nets:
  N1: Part1.D9_PWM, J1.pulse
  GND: Part1.GND, J1.gnd
  VIN: Part1.VIN, J1.vcc
  N2: Part2.5V, S1.2, S2.2
  N3: Part2.GND, R1.Pin_1, R2.Pin_1
  N4: Part2.D2_PWM, S2.3
  N5: Part2.D3_PWM, S1.3
  N6: S1.4, R1.Pin_0
  N7: S2.4, R2.Pin_0
